# Fritzing sketch remedio-certo (saved by Fritzing 0.9.2b)

parts:
  U1 = NodeMCU V1.0
  Squix1 = OLED 0.96" 128x64 I2C SSD1306
  Part1 = KY-006 Passive Buzzer Module [package="Breakout board"]
  GY1 = MPU-6050 Board GY-521 [form="♀ (female)" package=THT]

nets:
  N1: U1.D0, Part1.S
  N2: U1.D1, GY1.pin3
  N3: U1.D2, GY1.pin4, GY1.pin5
  3V3: U1.3V3, Squix1.VCC, GY1.pin1
  GND: U1.GND, Squix1.GND, Part1.-, GY1.pin2
  N4: U1.D7, Squix1.SCL
  N5: U1.D8, Squix1.SCA

custom parts:
  NodeMCU V1.0: ESP8266 based NodeMCU
  KY-006 Passive Buzzer Module: Passive Piezoelectric Buzzer Module Keyes KY-006, it can produce a range of sound tones depending on the input frequency.
  MPU-6050 Board GY-521: Acelerometro y Giroscopio MPU-6050 Board GY-521
